# Fritzing sketch fritzing Home automation (saved by Fritzing 0.9.3b)

parts:
  8-Channel_Relay1 = 8-Channel 5v Relay Shield [package=relay-8ch5v10a]
  HLK-PM1 = HLK-PM01
  U1 = 4-Channel 5v Relay Shield [package=relay-4ch5v10a]
  M1 = DC Motor
  J1 = screw terminal, 12 pins
  LED1 = LEDs [package=led10mm]
  LED3 = LEDs [package=led10mm]
  C2 = Ceramic Capacitor [capacitance=100nF package="100 mil [THT, multilayer]"]
  C3 = Ceramic Capacitor [capacitance=100nF package="100 mil [THT, multilayer]"]
  C4 = Ceramic Capacitor [capacitance=100nF voltage=0.1kV package="100 mil [THT, multilayer]"]
  MH-ET_LIVE_ESP32_DEVKIT1 = MH-ET LIVE ESP32 DEVKIT 38 pins
  J2 = Screw terminal - 2 pins [package=THT]
  J3 = Screw terminal - 2 pins [package=THT]
  J4 = Screw terminal - 2 pins [package=THT]
  J5 = Screw terminal - 2 pins [package=THT]
  J6 = Screw terminal - 2 pins [package=THT]
  LED2 = LEDs [package=led10mm]

nets:
  VCC: 8-Channel_Relay1.VCC, HLK-PM1.+Vo, U1.VCC, MH-ET_LIVE_ESP32_DEVKIT1.5V
  GND: 8-Channel_Relay1.GND, HLK-PM1.-Vo, U1.GND, MH-ET_LIVE_ESP32_DEVKIT1.GND
  N1: 8-Channel_Relay1.IN1, MH-ET_LIVE_ESP32_DEVKIT1.IO13
  N2: 8-Channel_Relay1.IN2, MH-ET_LIVE_ESP32_DEVKIT1.IO12
  N3: 8-Channel_Relay1.IN3, MH-ET_LIVE_ESP32_DEVKIT1.IO14
  N4: 8-Channel_Relay1.IN4, MH-ET_LIVE_ESP32_DEVKIT1.IO27
  N5: 8-Channel_Relay1.IN5, MH-ET_LIVE_ESP32_DEVKIT1.IO26
  N6: 8-Channel_Relay1.IN6, MH-ET_LIVE_ESP32_DEVKIT1.IO25
  N7: 8-Channel_Relay1.IN7, MH-ET_LIVE_ESP32_DEVKIT1.IO33
  N8: 8-Channel_Relay1.K1-In, 8-Channel_Relay1.K2-In, 8-Channel_Relay1.K3-In, 8-Channel_Relay1.K4-In, 8-Channel_Relay1.K5-In, 8-Channel_Relay1.K6-In, 8-Channel_Relay1.K7-In, 8-Channel_Relay1.K8-In, HLK-PM1.AC, U1.K1-In, U1.K2-In, U1.K3-In, U1.K4-In, J2.pin2
  N9: 8-Channel_Relay1.K1-On, LED2.C
  N10: 8-Channel_Relay1.K2-On, LED1.C
  N11: 8-Channel_Relay1.K3-On, LED3.C
  N12: 8-Channel_Relay1.K4-On, J3.pin1
  N13: 8-Channel_Relay1.K5-On, J6.pin1
  N14: 8-Channel_Relay1.K6-On, J4.pin1
  N15: 8-Channel_Relay1.K7-On, J5.pin1
  N16: U1.IN1, MH-ET_LIVE_ESP32_DEVKIT1.IO19
  N17: U1.IN2, MH-ET_LIVE_ESP32_DEVKIT1.IO18
  N18: U1.K1-On, M1.pin_2, C2.0, C3.0, C4.0
  N19: U1.K2-On, C2.1
  N20: U1.IN4, MH-ET_LIVE_ESP32_DEVKIT1.IO16
  N21: U1.K3-On, C4.1
  N22: U1.K4-On, C3.1
  N23: U1.IN3, MH-ET_LIVE_ESP32_DEVKIT1.IO17
  N24: M1.pin_1, J1.pin2, J1.pin3, J1.pin4, J1.pin5, J1.pin6, J1.pin7, J1.pin8, J1.pin9, J1.pin10, J1.pin11, J1.pin12, LED1.A, LED3.A, J2.pin1, J3.pin2, J4.pin2, J5.pin2, J6.pin2, LED2.A

notes:
  Tubelight 1
  Tubelight 4
  Tubelight 3
  Tubelight 2

custom parts:
  8-Channel 5v Relay Shield: 8 Channel 5v Relay Shield w. 2x SPD-06VDC-SD-C
  4-Channel 5v Relay Shield: 4 Channel 5v Relay Shield w. 2x SPD-06VDC-SD-C
  LEDs: LEDs Standard schematic elements and footprints for 5mm, 3mm, 1206, and 0603 sized LEDs. 5mm - Spark Fun Electronics SKU : COM-00529 (and others)
  MH-ET LIVE ESP32 DEVKIT 38 pins: http://mh.nodebb.com/topic/2/mh-et-live-esp32-devkit
